# Fritzing sketch distance (saved by Fritzing 1.0.1rc)

parts:
  Mod1 = Raspberry Pi Pico W
  HC-SR04_Sensor_1 = HC-SR04 Ultrasonic Distance Sensor

nets:
  N1: Mod1.pin_16, HC-SR04_Sensor_1.TRIG
  N2: Mod1.pin_17, HC-SR04_Sensor_1.ECHO
  N3: Mod1.pin_23, Mod1.pin_33, HC-SR04_Sensor_1.GND
  N4: Mod1.pin_36, HC-SR04_Sensor_1.VCC

custom parts:
  Raspberry Pi Pico W: Raspberry Pi Pico W. Based around the RP2040 microcontroller the Pico W is a low cost microcontroller device bringing Raspberry Pi quality, cost, and easy of use to the microcontroller space. The areas marked KEEPOUT in pcb silkscreen should not have traces running through them to avoid shorts on a soldered in module!
